# Fritzing sketch circuit-diagram (saved by Fritzing 0.9.3b)
# 18650 Li-ion Battery: CC-BY Dr Kristofer Chan, King's College London/Remote-research.org

parts:
  ESP32_-_Back1 = ESP32 - CAM
  LED1 = LED - 3mm [color="Red (633nm)" package="3 mm [THT]"]
  LED2 = LED - 3mm [color="Green (555nm)" package="3 mm [THT]"]
  R1 = Resistor [tolerance=±5% resistance=220 package="2010 [SMD]"]
  R2 = Resistor [tolerance=±5% resistance=220 package="2010 [SMD]"]
  BAT1 = 18650 Li-ion Battery [package=battery-18650]
  MOD1 = MT3608 Boost No usb

nets:
  N1: ESP32_-_Back1.GPIO4, ESP32_-_Back1.GPIO2, R1.Pin_1
  N2: ESP32_-_Back1.GPIO14, R2.Pin_1
  N3: ESP32_-_Back1.GPIO12, ESP32_-_Back1.GND, LED1.cathode, LED2.cathode, BAT1.-, MOD1.IN_(-), MOD1.OUT_(-)
  N4: ESP32_-_Back1.5V, MOD1.OUT_(+)
  N5: LED1.anode, R2.Pin_0
  N6: LED2.anode, R1.Pin_0
  N7: BAT1.+, MOD1.IN_(+)

custom parts:
  ESP32 - CAM: The ESP32-CAM has a very competitive small-size camera module that can operate independently as a minimum system with a footprint of only 27*40.5*4.5mm and a deep sleep current of up to 6mA.
  18650 Li-ion Battery: 18650 li-ion Battery Standard 18650 battery with interactive connectors Creative Common Attribution 4.0 International (CC-BY 4.0) license. Any use of this part requires attribution of Dr Kristofer Chan, Department of Geography, King's College London. Contact kristofer.chan [at] kcl.ac.uk OR kris [at] remote-research.org for further information.
  MT3608 Boost No usb: Chip- MT3608 / B6289 DC to DC step up, power booster module. With adjustable output voltage. Current- 2A . || Input voltage- 2V-24V || Output voltage- 5V-28V Input interface- Inversed polarity- NO. || Led indicator- No.
